# Fritzing sketch Circuit (saved by Fritzing 0.9.4)
breadboards: 1

parts:
  Raspberry_Pi_1 = Raspberry Pi 3 [part_number=RPI-3-V1.2]
  Monk_Makes_Servo_Six_Board1 = Monk Makes Servo Six Board [part_number="Servo Six Board v1.0d"]
  R1 = Resistor [tolerance=±5% resistance=220 package=THT]
  LED1 = LED - 5mm [color="Red (633nm)" package="5 mm [THT]"]
  S1 = Pushbutton [package="[THT]"]
  J1 = Basic Servo
  J2 = Basic Servo
  J3 = Basic Servo
  VCC1 = 4 x AAA Battery Mount

nets:
  GND: Raspberry_Pi_1.GND, Monk_Makes_Servo_Six_Board1.IN-GND, Monk_Makes_Servo_Six_Board1.PSU-GND, Monk_Makes_Servo_Six_Board1.OUT-1-GND, Monk_Makes_Servo_Six_Board1.OUT-2-GND, Monk_Makes_Servo_Six_Board1.OUT-3-GND, LED1.cathode, S1.Pin_3, S1.Pin_4, J1.gnd, J2.gnd, J3.gnd, VCC1.-
  N1: Raspberry_Pi_1.GIPO27, Monk_Makes_Servo_Six_Board1.IN-3
  N2: Raspberry_Pi_1.GIPO19, Monk_Makes_Servo_Six_Board1.IN-2
  N3: Raspberry_Pi_1.GIPO7, S1.Pin_1, S1.Pin_2
  N4: Raspberry_Pi_1.GIPO18, Monk_Makes_Servo_Six_Board1.IN-1
  N5: Raspberry_Pi_1.GIPO15, R1.Pin_1
  VCC: Monk_Makes_Servo_Six_Board1.PSU-VCC, Monk_Makes_Servo_Six_Board1.OUT-1-VCC, Monk_Makes_Servo_Six_Board1.OUT-2-VCC, Monk_Makes_Servo_Six_Board1.OUT-3-VCC, J1.vcc, J2.vcc, J3.vcc, VCC1.+
  N6: Monk_Makes_Servo_Six_Board1.OUT-1-CONTROL, J1.pulse
  N7: Monk_Makes_Servo_Six_Board1.OUT-2-CONTROL, J2.pulse
  N8: Monk_Makes_Servo_Six_Board1.OUT-3-CONTROL, J3.pulse
  N9: R1.Pin_0, LED1.anode

custom parts:
  Monk Makes Servo Six Board: The Servo Six Board by Monk Makes simplifies the process of connecting up to six servo motors to a Raspberry Pi or Arduino.
